// Digital circuit Two_bit_adder.dig as structural Verilog
module Two_bit_adder (
  input  A0,
  input  B0,
  input  A1,
  input  B1,
  input  clk,
  input  clk_2
);

  wire [2:0] fpga_ckt_1_p5;

  Seven_Seg_Hex seven_seg_hex_1 (.d({2'b00, A1, A0}), .dp(1'b0));
  Seven_Seg_Hex seven_seg_hex_2 (.d({2'b00, B1, B0}), .dp(1'b0));
  Seven_Seg_Hex seven_seg_hex_3 (.d({1'b0, fpga_ckt_1_p5}), .dp(1'b0));
  // fpga_ckt fpga_ckt_1: pin names not known; wires that end beside it: A0, B0, A1, B1, fpga_ckt_1_p5[0], fpga_ckt_1_p5[1], fpga_ckt_1_p5[2], clk, clk_2

  // Other names for the same wires on the sheet: sclk = clk_2

  // Notes on the sheet:
  //   clk_2: Hz: 5000
endmodule
