// Digital circuit async_counter_3bit.dig as structural Verilog
module async_counter_3bit (
  input  clk,
  input  clk_2,
  output Q0,
  output Q1,
  output Q2
);

  fpga_ckt fpga_ckt_1 ();  // open: clk, p0, p1, p2, p3, p4, p5, p6, p7, p8, p9, p10, p11, p12, p13, p14, p15, p16, p17, p18, p19, p20, p21, p22, p23, sys_clk
  Seven_Seg_Hex seven_seg_hex_1 (.d({1'b0, Q2, Q1, Q0}), .dp(1'b0));

  // Other names for the same wires on the sheet: sclk = clk_2

  // Notes on the sheet:
  //   clk: Hz: 2
  //   clk_2: Hz: 5000
endmodule
