// Digital circuit bidir_buf.dig as structural Verilog
module bidir_buf (
  input  left,
  input  right,
  input  dir,
  input  en
);

  wire and_1_out, and_2_out;

  NFET nfet_1 (.G(and_2_out), .D(left), .S(right));
  and and_1 (and_1_out, ~dir, en);  // And
  NFET nfet_2 (.G(and_1_out), .D(right), .S(left));
  and and_2 (and_2_out, dir, en);
endmodule
