// Digital circuit connection_box.dig as structural Verilog
module connection_box (
  input  in,
  input  Si,
  input  clk,
  output u0,
  output d0,
  output u1,
  output d1,
  output u2,
  output d2,
  output u3,
  output d3,
  output So
);

  wire dir0, dir1, dir2, dir3, shift_reg_4bit_1_o;
  wire [3:0] shift_reg_4bit_1_d;

  shift_reg_4bit shift_reg_4bit_1 (.i(Si), .c(clk), .o(shift_reg_4bit_1_o), .d(shift_reg_4bit_1_d));
  shift_reg_4bit shift_reg_4bit_2 (.i(shift_reg_4bit_1_o), .c(clk), .o(So), .d({dir3, dir2, dir1, dir0}));
  bidir_buf bidir_buf_1 (.left(d0), .right(in), .dir(dir0), .en(shift_reg_4bit_1_d[0]));
  bidir_buf bidir_buf_2 (.left(d1), .right(in), .dir(dir1), .en(shift_reg_4bit_1_d[1]));
  bidir_buf bidir_buf_3 (.left(d2), .right(in), .dir(dir2), .en(shift_reg_4bit_1_d[2]));
  bidir_buf bidir_buf_4 (.left(d3), .right(in), .dir(dir3), .en(shift_reg_4bit_1_d[3]));

  assign u0 = d0;
  assign u1 = d1;
  assign u2 = d2;
  assign u3 = d3;
endmodule
