// Digital circuit fpga_ckt.dig as structural Verilog
module fpga_ckt (
  input  clk,
  input  p0,
  input  p1,
  input  p2,
  input  p3,
  input  p4,
  input  p5,
  input  p6,
  input  p7,
  input  p8,
  input  p9,
  input  p10,
  input  p11,
  input  p12,
  input  p13,
  input  p14,
  input  p15,
  input  p16,
  input  p17,
  input  p18,
  input  p19,
  input  p20,
  input  p21,
  input  p22,
  input  p23,
  input  sys_clk
);

  wire c0, c1, c2, c3, c4, c5, c6, c7, c8, c9, c10, c11, c12, c13, c14, c15, c16, c17, c18, c19, c20, c21,
       c22, c23, c24, c25, c26, c27, c28, c29, c30, c31, c32, c33, c34, c35, c36, c37, c38, c39, c40, c41,
       clk_t, connection_box_1_d0, connection_box_1_d1, connection_box_1_d2, connection_box_1_d3,
       connection_box_1_u1, connection_box_1_u2, connection_box_1_u3, connection_box_2_d0,
       connection_box_2_d1, connection_box_2_d2, connection_box_2_d3, connection_box_3_d0,
       connection_box_3_d1, connection_box_3_d2, connection_box_3_d3, connection_box_3_u1,
       connection_box_3_u2, connection_box_3_u3, connection_box_4_d0, connection_box_4_d1,
       connection_box_4_d2, connection_box_4_d3, connection_box_5_d0, connection_box_5_d1,
       connection_box_5_d2, connection_box_5_d3, connection_box_5_u1, connection_box_5_u2,
       connection_box_5_u3, connection_box_6_d0, connection_box_6_d1, connection_box_6_d2,
       connection_box_6_d3, connection_box_7_d0, connection_box_7_d1, connection_box_7_d2,
       connection_box_7_d3, connection_box_8_u0, connection_box_8_u1, connection_box_8_u2,
       connection_box_8_u3, connection_box_9_u0, connection_box_9_u1, connection_box_9_u2,
       connection_box_9_u3, connection_box_10_d0, connection_box_10_d1, connection_box_10_d2,
       connection_box_10_d3, connection_box_11_d0, connection_box_11_d1, connection_box_11_d2,
       connection_box_11_d3, connection_box_11_u1, connection_box_11_u2, connection_box_11_u3,
       connection_box_12_d0, connection_box_12_d1, connection_box_12_d2, connection_box_12_d3,
       connection_box_13_d0, connection_box_13_d1, connection_box_13_d2, connection_box_13_d3,
       connection_box_13_u1, connection_box_13_u2, connection_box_13_u3, connection_box_14_d0,
       connection_box_14_d1, connection_box_14_d2, connection_box_14_d3, connection_box_15_d0,
       connection_box_15_d1, connection_box_15_d2, connection_box_15_d3, connection_box_15_u1,
       connection_box_15_u2, connection_box_15_u3, connection_box_16_d0, connection_box_16_d1,
       connection_box_16_d2, connection_box_16_d3, connection_box_17_d0, connection_box_17_d1,
       connection_box_17_d2, connection_box_17_d3, connection_box_18_u0, connection_box_18_u1,
       connection_box_18_u2, connection_box_18_u3, connection_box_19_u0, connection_box_19_u1,
       connection_box_19_u2, connection_box_19_u3, connection_box_20_d0, connection_box_20_d1,
       connection_box_20_d2, connection_box_20_d3, connection_box_21_d0, connection_box_21_d1,
       connection_box_21_d2, connection_box_21_d3, connection_box_21_u1, connection_box_21_u2,
       connection_box_21_u3, connection_box_22_d0, connection_box_22_d1, connection_box_22_d2,
       connection_box_22_d3, connection_box_23_d0, connection_box_23_d1, connection_box_23_d2,
       connection_box_23_d3, connection_box_23_u1, connection_box_23_u2, connection_box_23_u3,
       connection_box_24_d0, connection_box_24_d1, connection_box_24_d2, connection_box_24_d3,
       connection_box_25_d0, connection_box_25_d1, connection_box_25_d2, connection_box_25_d3,
       connection_box_25_u1, connection_box_25_u2, connection_box_25_u3, connection_box_26_d0,
       connection_box_26_d1, connection_box_26_d2, connection_box_26_d3, connection_box_27_d0,
       connection_box_27_d1, connection_box_27_d2, connection_box_27_d3, connection_box_28_u0,
       connection_box_28_u1, connection_box_28_u2, connection_box_28_u3, connection_box_29_u0,
       connection_box_29_u1, connection_box_29_u2, connection_box_29_u3, connection_box_30_d0,
       connection_box_30_d1, connection_box_30_d2, connection_box_30_d3, connection_box_31_d0,
       connection_box_31_d1, connection_box_31_d2, connection_box_31_d3, connection_box_31_u1,
       connection_box_31_u2, connection_box_31_u3, connection_box_32_d0, connection_box_32_d1,
       connection_box_32_d2, connection_box_32_d3, connection_box_32_u0, connection_box_32_u1,
       connection_box_32_u2, connection_box_32_u3, connection_box_33_d0, connection_box_33_d1,
       connection_box_33_d2, connection_box_33_d3, connection_box_33_u1, connection_box_33_u2,
       connection_box_33_u3, connection_box_34_d0, connection_box_34_d1, connection_box_34_d2,
       connection_box_34_d3, connection_box_34_u0, connection_box_34_u1, connection_box_34_u2,
       connection_box_34_u3, connection_box_35_d0, connection_box_35_d1, connection_box_35_d2,
       connection_box_35_d3, connection_box_35_u1, connection_box_35_u2, connection_box_35_u3,
       connection_box_36_d0, connection_box_36_d1, connection_box_36_d2, connection_box_36_d3,
       connection_box_36_u0, connection_box_36_u1, connection_box_36_u2, connection_box_36_u3,
       connection_box_37_u0, connection_box_37_u1, connection_box_37_u2, connection_box_37_u3,
       connection_box_39_u0, connection_box_39_u1, connection_box_39_u2, connection_box_39_u3,
       connection_box_41_u0, connection_box_41_u1, connection_box_41_u2, connection_box_41_u3, d0, d1, d2,
       d3, d4, d5, d6, d7, d8, in, load_over, nfet_1_d, nfet_2_d, nfet_3_d, nfet_4_d, nfet_5_d, nfet_6_d,
       nfet_7_s, nfet_8_d, nfet_9_s, nfet_10_d, nfet_11_d, nfet_12_d, nfet_13_d, nfet_14_d, nfet_15_d,
       nfet_16_d, nfet_17_s, nfet_18_d, nfet_19_s, nfet_20_d, nfet_21_d, nfet_22_d, nfet_23_d, nfet_24_d,
       nfet_25_d, nfet_26_d, nfet_27_s, nfet_28_d, nfet_29_s, nfet_30_d, nfet_31_d, nfet_32_d, nfet_33_d,
       nfet_34_d, nfet_35_d, nfet_36_d, nfet_37_d, nfet_38_d, nfet_39_d, nfet_40_s, nfet_41_s, nfet_42_s,
       not_1_out, not_2_out, out, s1, s2, s3, s4, s5, s6, s7, s8, s9, s10, s11, s12, s13, s14, s15,
       slice_block_1_y1, slice_block_1_y2, slice_block_2_y1, slice_block_2_y2, slice_block_3_y1,
       slice_block_3_y2, slice_block_4_y1, slice_block_4_y2, slice_block_5_y1, slice_block_5_y2,
       slice_block_6_y1, slice_block_6_y2, slice_block_7_y1, slice_block_7_y2, slice_block_8_y1,
       slice_block_8_y2, slice_block_9_y1, slice_block_9_y2, switch_block_1_d, switch_block_1_r,
       switch_block_2_d, switch_block_2_r, switch_block_3_d, switch_block_3_r, switch_block_4_r,
       switch_block_5_r, switch_block_5_so, switch_block_6_r, switch_block_6_so, switch_block_7_r,
       switch_block_7_so, switch_block_8_r, switch_block_9_r, switch_block_9_so, switch_block_10_r,
       switch_block_10_so, switch_block_11_r, switch_block_11_so, switch_block_12_r, switch_block_13_r,
       switch_block_13_so, switch_block_14_r, switch_block_14_so, switch_block_15_r, switch_block_15_so,
       switch_block_16_r, switch_block_17_d, switch_block_17_r, switch_block_18_d, switch_block_18_r,
       switch_block_19_d, switch_block_19_r, switch_block_20_r, switch_block_21_r, switch_block_21_so,
       switch_block_22_r, switch_block_22_so, switch_block_23_r, switch_block_23_so, switch_block_24_r,
       switch_block_24_so, switch_block_25_r, switch_block_25_so, switch_block_26_r, switch_block_26_so,
       switch_block_27_r, switch_block_27_so, switch_block_28_r, switch_block_28_so, switch_block_29_r,
       switch_block_29_so, switch_block_30_r, switch_block_30_so, switch_block_31_r, switch_block_31_so,
       switch_block_32_r, switch_block_32_so, switch_block_33_d, switch_block_33_r, switch_block_34_d,
       switch_block_34_r, switch_block_35_d, switch_block_35_r, switch_block_36_r, switch_block_37_r,
       switch_block_37_so, switch_block_38_r, switch_block_38_so, switch_block_39_r, switch_block_39_so,
       switch_block_40_r, switch_block_40_so, switch_block_41_r, switch_block_41_so, switch_block_42_r,
       switch_block_42_so, switch_block_43_r, switch_block_43_so, switch_block_44_r, switch_block_44_so,
       switch_block_45_r, switch_block_45_so, switch_block_46_r, switch_block_46_so, switch_block_47_r,
       switch_block_47_so, switch_block_48_r, switch_block_48_so, switch_block_49_d, switch_block_50_d,
       switch_block_51_d, switch_block_54_so, switch_block_55_so, switch_block_58_so, switch_block_59_so,
       switch_block_62_so, switch_block_63_so;
  wire [10:0] counter_1_out;

  not not_1 (not_1_out, load_over);
  not not_2 (not_2_out, clk_t);
  and and_1 (clk_t, not_1_out, sys_clk);
  Counter #(.Bits(11), .isProgramCounter("true")) counter_1 (
    .en(not_1_out), .C(not_2_out), .clr(1'b0), .out(counter_1_out));  // open: ovf
  Comparator #(.Bits(11)) comparator_1 (.a(11'h595), .b(counter_1_out), .eq(load_over));  // open: gt, lt
  ROM #(.AddrBits(11)) bitstream (.A(counter_1_out), .sel(1'b1), .D(in));
  NFET nfet_1 (.G(load_over), .D(nfet_1_d), .S(p0));
  NFET nfet_2 (.G(load_over), .D(nfet_2_d), .S(p1));
  NFET nfet_3 (.G(load_over), .D(nfet_3_d), .S(p2));
  NFET nfet_4 (.G(load_over), .D(nfet_4_d), .S(p3));
  NFET nfet_5 (.G(load_over), .D(nfet_5_d), .S(p4));
  NFET nfet_6 (.G(load_over), .D(nfet_6_d), .S(p5));
  switch_block switch_block_1 (
    .R(switch_block_1_r), .D(switch_block_1_d), .clk(clk_t), .Si(switch_block_5_so), .So(c23));  // open: L, U
  connection_box connection_box_1 (
    .in(nfet_1_d), .Si(c0), .clk(clk_t), .u0(switch_block_1_d), .d0(connection_box_1_d0),
    .u1(connection_box_1_u1), .d1(connection_box_1_d1), .u2(connection_box_1_u2), .d2(connection_box_1_d2),
    .u3(connection_box_1_u3), .d3(connection_box_1_d3), .So(c1));
  connection_box connection_box_2 (
    .in(nfet_2_d), .Si(c1), .clk(clk_t), .u0(connection_box_1_d0), .d0(connection_box_2_d0),
    .u1(connection_box_1_d1), .d1(connection_box_2_d1), .u2(connection_box_1_d2), .d2(connection_box_2_d2),
    .u3(connection_box_1_d3), .d3(connection_box_2_d3), .So(s4));
  switch_block switch_block_2 (
    .R(switch_block_2_r), .U(connection_box_2_d0), .D(switch_block_2_d), .clk(clk_t), .Si(switch_block_6_so),
    .So(s5));  // open: L
  connection_box connection_box_3 (
    .in(nfet_3_d), .Si(c2), .clk(clk_t), .u0(switch_block_2_d), .d0(connection_box_3_d0),
    .u1(connection_box_3_u1), .d1(connection_box_3_d1), .u2(connection_box_3_u2), .d2(connection_box_3_d2),
    .u3(connection_box_3_u3), .d3(connection_box_3_d3), .So(c3));
  connection_box connection_box_4 (
    .in(nfet_4_d), .Si(c3), .clk(clk_t), .u0(connection_box_3_d0), .d0(connection_box_4_d0),
    .u1(connection_box_3_d1), .d1(connection_box_4_d1), .u2(connection_box_3_d2), .d2(connection_box_4_d2),
    .u3(connection_box_3_d3), .d3(connection_box_4_d3), .So(s8));
  switch_block switch_block_3 (
    .R(switch_block_3_r), .U(connection_box_4_d0), .D(switch_block_3_d), .clk(clk_t), .Si(switch_block_7_so),
    .So(s9));  // open: L
  connection_box connection_box_5 (
    .in(nfet_5_d), .Si(c4), .clk(clk_t), .u0(switch_block_3_d), .d0(connection_box_5_d0),
    .u1(connection_box_5_u1), .d1(connection_box_5_d1), .u2(connection_box_5_u2), .d2(connection_box_5_d2),
    .u3(connection_box_5_u3), .d3(connection_box_5_d3), .So(c5));
  connection_box connection_box_6 (
    .in(nfet_6_d), .Si(c5), .clk(clk_t), .u0(connection_box_5_d0), .d0(connection_box_6_d0),
    .u1(connection_box_5_d1), .d1(connection_box_6_d1), .u2(connection_box_5_d2), .d2(connection_box_6_d2),
    .u3(connection_box_5_d3), .d3(connection_box_6_d3), .So(s12));
  switch_block switch_block_4 (.R(switch_block_4_r), .U(connection_box_6_d0), .clk(clk_t), .So(c6));  // open: L, D, Si
  switch_block switch_block_5 (
    .R(switch_block_5_r), .D(connection_box_1_u1), .clk(clk_t), .Si(switch_block_9_so), .So(switch_block_5_so));  // open: L, U
  switch_block switch_block_6 (
    .R(switch_block_6_r), .U(connection_box_2_d1), .D(connection_box_3_u1), .clk(clk_t),
    .Si(switch_block_10_so), .So(switch_block_6_so));  // open: L
  switch_block switch_block_7 (
    .R(switch_block_7_r), .U(connection_box_4_d1), .D(connection_box_5_u1), .clk(clk_t),
    .Si(switch_block_11_so), .So(switch_block_7_so));  // open: L
  switch_block switch_block_8 (.R(switch_block_8_r), .U(connection_box_6_d1), .clk(clk_t));  // open: L, D, cfg
  switch_block switch_block_9 (
    .R(switch_block_9_r), .D(connection_box_1_u2), .clk(clk_t), .Si(switch_block_13_so),
    .So(switch_block_9_so));  // open: L, U
  switch_block switch_block_10 (
    .R(switch_block_10_r), .U(connection_box_2_d2), .D(connection_box_3_u2), .clk(clk_t),
    .Si(switch_block_14_so), .So(switch_block_10_so));  // open: L
  switch_block switch_block_11 (
    .R(switch_block_11_r), .U(connection_box_4_d2), .D(connection_box_5_u2), .clk(clk_t),
    .Si(switch_block_15_so), .So(switch_block_11_so));  // open: L
  switch_block switch_block_12 (.R(switch_block_12_r), .U(connection_box_6_d2), .clk(clk_t));  // open: L, D, cfg
  switch_block switch_block_13 (
    .R(switch_block_13_r), .D(connection_box_1_u3), .clk(clk_t), .Si(in), .So(switch_block_13_so));  // open: L, U
  switch_block switch_block_14 (
    .R(switch_block_14_r), .U(connection_box_2_d3), .D(connection_box_3_u3), .clk(clk_t), .Si(s4),
    .So(switch_block_14_so));  // open: L
  switch_block switch_block_15 (
    .R(switch_block_15_r), .U(connection_box_4_d3), .D(connection_box_5_u3), .clk(clk_t), .Si(s8),
    .So(switch_block_15_so));  // open: L
  switch_block switch_block_16 (
    .R(switch_block_16_r), .U(connection_box_6_d3), .clk(clk_t), .Si(s12));  // open: L, D, So
  NFET nfet_7 (.G(load_over), .D(p23), .S(nfet_7_s));
  slice_block slice_block_1 (
    .A0(connection_box_1_u3), .A3(connection_box_1_d0), .A1(connection_box_1_d2), .A2(connection_box_1_d1),
    .B0(switch_block_13_r), .B1(connection_box_8_u1), .B2(connection_box_8_u2), .B3(connection_box_9_u3),
    .C0(switch_block_14_r), .C1(switch_block_10_r), .C2(switch_block_6_r), .C3(switch_block_2_r),
    .clk0(switch_block_14_r), .clk1(switch_block_10_r), .clk2(switch_block_6_r), .Y1(slice_block_1_y1),
    .Y2(slice_block_1_y2), .clk(clk_t), .Si(d0), .So(c0), .f_clk(clk));  // open: data
  slice_block slice_block_2 (
    .A0(connection_box_3_u3), .A3(connection_box_3_d0), .A1(connection_box_3_d2), .A2(connection_box_3_d1),
    .B0(switch_block_14_r), .B1(switch_block_10_r), .B2(switch_block_6_r), .B3(switch_block_2_r),
    .C0(switch_block_15_r), .C1(switch_block_11_r), .C2(switch_block_7_r), .C3(switch_block_3_r),
    .clk0(switch_block_15_r), .clk1(switch_block_11_r), .clk2(switch_block_7_r), .Y1(slice_block_2_y1),
    .Y2(slice_block_2_y2), .clk(clk_t), .Si(d3), .So(c2), .f_clk(clk));  // open: data
  slice_block slice_block_3 (
    .A0(connection_box_5_u3), .A3(connection_box_5_d0), .A1(connection_box_5_d2), .A2(connection_box_5_d1),
    .B0(switch_block_15_r), .B1(switch_block_11_r), .B2(switch_block_7_r), .B3(switch_block_3_r),
    .C0(connection_box_7_d3), .C1(connection_box_7_d2), .C2(connection_box_7_d1), .C3(connection_box_10_d0),
    .clk0(switch_block_16_r), .clk1(switch_block_12_r), .clk2(switch_block_8_r), .Y1(slice_block_3_y1),
    .Y2(slice_block_3_y2), .clk(clk_t), .Si(d6), .So(c4), .f_clk(clk));  // open: data
  connection_box connection_box_7 (
    .in(nfet_8_d), .Si(c6), .clk(clk_t), .u0(switch_block_4_r), .d0(connection_box_7_d0),
    .u1(switch_block_8_r), .d1(connection_box_7_d1), .u2(switch_block_12_r), .d2(connection_box_7_d2),
    .u3(switch_block_16_r), .d3(connection_box_7_d3), .So(c7));
  NFET nfet_8 (.G(load_over), .D(nfet_8_d), .S(p6));
  connection_box connection_box_8 (
    .in(nfet_7_s), .Si(c23), .clk(clk_t), .u0(connection_box_8_u0), .d0(switch_block_13_r),
    .u1(connection_box_8_u1), .d1(switch_block_9_r), .u2(connection_box_8_u2), .d2(switch_block_5_r),
    .u3(connection_box_8_u3), .d3(switch_block_1_r), .So(c22));
  NFET nfet_9 (.G(load_over), .D(p22), .S(nfet_9_s));
  connection_box connection_box_9 (
    .in(nfet_9_s), .Si(c22), .clk(clk_t), .u0(connection_box_9_u0), .d0(connection_box_8_u0),
    .u1(connection_box_9_u1), .d1(connection_box_8_u1), .u2(connection_box_9_u2), .d2(connection_box_8_u2),
    .u3(connection_box_9_u3), .d3(connection_box_8_u3), .So(s1));
  connection_box connection_box_10 (
    .in(nfet_10_d), .Si(c7), .clk(clk_t), .u0(connection_box_7_d0), .d0(connection_box_10_d0),
    .u1(connection_box_7_d1), .d1(connection_box_10_d1), .u2(connection_box_7_d2), .d2(connection_box_10_d2),
    .u3(connection_box_7_d3), .d3(connection_box_10_d3), .So(s13));
  NFET nfet_10 (.G(load_over), .D(nfet_10_d), .S(p7));
  NFET nfet_11 (.G(load_over), .D(nfet_11_d), .S(slice_block_1_y1));
  NFET nfet_12 (.G(load_over), .D(nfet_12_d), .S(slice_block_1_y2));
  NFET nfet_13 (.G(load_over), .D(nfet_13_d), .S(slice_block_2_y1));
  NFET nfet_14 (.G(load_over), .D(nfet_14_d), .S(slice_block_2_y2));
  NFET nfet_15 (.G(load_over), .D(nfet_15_d), .S(slice_block_3_y1));
  NFET nfet_16 (.G(load_over), .D(nfet_16_d), .S(slice_block_3_y2));
  switch_block switch_block_17 (
    .R(switch_block_17_r), .L(connection_box_9_u3), .D(switch_block_17_d), .clk(clk_t),
    .Si(switch_block_21_so), .So(c21));  // open: U
  connection_box connection_box_11 (
    .in(nfet_11_d), .Si(c24), .clk(clk_t), .u0(switch_block_17_d), .d0(connection_box_11_d0),
    .u1(connection_box_11_u1), .d1(connection_box_11_d1), .u2(connection_box_11_u2),
    .d2(connection_box_11_d2), .u3(connection_box_11_u3), .d3(connection_box_11_d3), .So(c25));
  connection_box connection_box_12 (
    .in(nfet_12_d), .Si(c25), .clk(clk_t), .u0(connection_box_11_d0), .d0(connection_box_12_d0),
    .u1(connection_box_11_d1), .d1(connection_box_12_d1), .u2(connection_box_11_d2),
    .d2(connection_box_12_d2), .u3(connection_box_11_d3), .d3(connection_box_12_d3), .So(d0));
  switch_block switch_block_18 (
    .R(switch_block_18_r), .L(switch_block_2_r), .U(connection_box_12_d0), .D(switch_block_18_d),
    .clk(clk_t), .Si(switch_block_22_so), .So(s6));
  connection_box connection_box_13 (
    .in(nfet_13_d), .Si(c30), .clk(clk_t), .u0(switch_block_18_d), .d0(connection_box_13_d0),
    .u1(connection_box_13_u1), .d1(connection_box_13_d1), .u2(connection_box_13_u2),
    .d2(connection_box_13_d2), .u3(connection_box_13_u3), .d3(connection_box_13_d3), .So(c31));
  connection_box connection_box_14 (
    .in(nfet_14_d), .Si(c31), .clk(clk_t), .u0(connection_box_13_d0), .d0(connection_box_14_d0),
    .u1(connection_box_13_d1), .d1(connection_box_14_d1), .u2(connection_box_13_d2),
    .d2(connection_box_14_d2), .u3(connection_box_13_d3), .d3(connection_box_14_d3), .So(d3));
  switch_block switch_block_19 (
    .R(switch_block_19_r), .L(switch_block_3_r), .U(connection_box_14_d0), .D(switch_block_19_d),
    .clk(clk_t), .Si(switch_block_23_so), .So(s10));
  connection_box connection_box_15 (
    .in(nfet_15_d), .Si(c36), .clk(clk_t), .u0(switch_block_19_d), .d0(connection_box_15_d0),
    .u1(connection_box_15_u1), .d1(connection_box_15_d1), .u2(connection_box_15_u2),
    .d2(connection_box_15_d2), .u3(connection_box_15_u3), .d3(connection_box_15_d3), .So(c37));
  connection_box connection_box_16 (
    .in(nfet_16_d), .Si(c37), .clk(clk_t), .u0(connection_box_15_d0), .d0(connection_box_16_d0),
    .u1(connection_box_15_d1), .d1(connection_box_16_d1), .u2(connection_box_15_d2),
    .d2(connection_box_16_d2), .u3(connection_box_15_d3), .d3(connection_box_16_d3), .So(d6));
  switch_block switch_block_20 (
    .R(switch_block_20_r), .L(connection_box_10_d0), .U(connection_box_16_d0), .clk(clk_t),
    .Si(switch_block_24_so), .So(c8));  // open: D
  switch_block switch_block_21 (
    .R(switch_block_21_r), .L(connection_box_9_u2), .D(connection_box_11_u1), .clk(clk_t),
    .Si(switch_block_25_so), .So(switch_block_21_so));  // open: U
  switch_block switch_block_22 (
    .R(switch_block_22_r), .L(switch_block_6_r), .U(connection_box_12_d1), .D(connection_box_13_u1),
    .clk(clk_t), .Si(switch_block_26_so), .So(switch_block_22_so));
  switch_block switch_block_23 (
    .R(switch_block_23_r), .L(switch_block_7_r), .U(connection_box_14_d1), .D(connection_box_15_u1),
    .clk(clk_t), .Si(switch_block_27_so), .So(switch_block_23_so));
  switch_block switch_block_24 (
    .R(switch_block_24_r), .L(connection_box_10_d1), .U(connection_box_16_d1), .clk(clk_t),
    .Si(switch_block_28_so), .So(switch_block_24_so));  // open: D
  switch_block switch_block_25 (
    .R(switch_block_25_r), .L(connection_box_9_u1), .D(connection_box_11_u2), .clk(clk_t),
    .Si(switch_block_29_so), .So(switch_block_25_so));  // open: U
  switch_block switch_block_26 (
    .R(switch_block_26_r), .L(switch_block_10_r), .U(connection_box_12_d2), .D(connection_box_13_u2),
    .clk(clk_t), .Si(switch_block_30_so), .So(switch_block_26_so));
  switch_block switch_block_27 (
    .R(switch_block_27_r), .L(switch_block_11_r), .U(connection_box_14_d2), .D(connection_box_15_u2),
    .clk(clk_t), .Si(switch_block_31_so), .So(switch_block_27_so));
  switch_block switch_block_28 (
    .R(switch_block_28_r), .L(connection_box_10_d2), .U(connection_box_16_d2), .clk(clk_t),
    .Si(switch_block_32_so), .So(switch_block_28_so));  // open: D
  switch_block switch_block_29 (
    .R(switch_block_29_r), .L(connection_box_9_u0), .D(connection_box_11_u3), .clk(clk_t), .Si(s1),
    .So(switch_block_29_so));  // open: U
  switch_block switch_block_30 (
    .R(switch_block_30_r), .L(switch_block_14_r), .U(connection_box_12_d3), .D(connection_box_13_u3),
    .clk(clk_t), .Si(s5), .So(switch_block_30_so));
  switch_block switch_block_31 (
    .R(switch_block_31_r), .L(switch_block_15_r), .U(connection_box_14_d3), .D(connection_box_15_u3),
    .clk(clk_t), .Si(s9), .So(switch_block_31_so));
  switch_block switch_block_32 (
    .R(switch_block_32_r), .L(connection_box_10_d3), .U(connection_box_16_d3), .clk(clk_t), .Si(s13),
    .So(switch_block_32_so));  // open: D
  NFET nfet_17 (.G(load_over), .D(p21), .S(nfet_17_s));
  slice_block slice_block_4 (
    .A0(connection_box_11_u3), .A3(connection_box_11_d0), .A1(connection_box_11_d2),
    .A2(connection_box_11_d1), .B0(switch_block_29_r), .B1(connection_box_18_u1), .B2(connection_box_18_u2),
    .B3(connection_box_19_u3), .C0(switch_block_30_r), .C1(switch_block_26_r), .C2(switch_block_22_r),
    .C3(switch_block_18_r), .clk0(switch_block_30_r), .clk1(switch_block_26_r), .clk2(switch_block_22_r),
    .Y1(slice_block_4_y1), .Y2(slice_block_4_y2), .clk(clk_t), .Si(d1), .So(c24), .f_clk(clk));  // open: data
  slice_block slice_block_5 (
    .A0(connection_box_13_u3), .A3(connection_box_13_d0), .A1(connection_box_13_d2),
    .A2(connection_box_13_d1), .B0(switch_block_30_r), .B1(switch_block_26_r), .B2(switch_block_22_r),
    .B3(switch_block_18_r), .C0(switch_block_31_r), .C1(switch_block_27_r), .C2(switch_block_23_r),
    .C3(switch_block_19_r), .clk0(switch_block_31_r), .clk1(switch_block_27_r), .clk2(switch_block_23_r),
    .Y1(slice_block_5_y1), .Y2(slice_block_5_y2), .clk(clk_t), .Si(d4), .So(c30), .f_clk(clk));  // open: data
  slice_block slice_block_6 (
    .A0(connection_box_15_u3), .A3(connection_box_15_d0), .A1(connection_box_15_d2),
    .A2(connection_box_15_d1), .B0(switch_block_31_r), .B1(switch_block_27_r), .B2(switch_block_23_r),
    .B3(switch_block_19_r), .C0(connection_box_17_d3), .C1(connection_box_17_d2), .C2(connection_box_17_d1),
    .C3(connection_box_20_d0), .clk0(switch_block_32_r), .clk1(switch_block_28_r), .clk2(switch_block_24_r),
    .Y1(slice_block_6_y1), .Y2(slice_block_6_y2), .clk(clk_t), .Si(d7), .So(c36), .f_clk(clk));  // open: data
  connection_box connection_box_17 (
    .in(nfet_18_d), .Si(c8), .clk(clk_t), .u0(switch_block_20_r), .d0(connection_box_17_d0),
    .u1(switch_block_24_r), .d1(connection_box_17_d1), .u2(switch_block_28_r), .d2(connection_box_17_d2),
    .u3(switch_block_32_r), .d3(connection_box_17_d3), .So(c9));
  NFET nfet_18 (.G(load_over), .D(nfet_18_d), .S(p8));
  connection_box connection_box_18 (
    .in(nfet_17_s), .Si(c21), .clk(clk_t), .u0(connection_box_18_u0), .d0(switch_block_29_r),
    .u1(connection_box_18_u1), .d1(switch_block_25_r), .u2(connection_box_18_u2), .d2(switch_block_21_r),
    .u3(connection_box_18_u3), .d3(switch_block_17_r), .So(c20));
  NFET nfet_19 (.G(load_over), .D(p20), .S(nfet_19_s));
  connection_box connection_box_19 (
    .in(nfet_19_s), .Si(c20), .clk(clk_t), .u0(connection_box_19_u0), .d0(connection_box_18_u0),
    .u1(connection_box_19_u1), .d1(connection_box_18_u1), .u2(connection_box_19_u2),
    .d2(connection_box_18_u2), .u3(connection_box_19_u3), .d3(connection_box_18_u3), .So(s2));
  connection_box connection_box_20 (
    .in(nfet_20_d), .Si(c9), .clk(clk_t), .u0(connection_box_17_d0), .d0(connection_box_20_d0),
    .u1(connection_box_17_d1), .d1(connection_box_20_d1), .u2(connection_box_17_d2),
    .d2(connection_box_20_d2), .u3(connection_box_17_d3), .d3(connection_box_20_d3), .So(s14));
  NFET nfet_20 (.G(load_over), .D(nfet_20_d), .S(p9));
  NFET nfet_21 (.G(load_over), .D(nfet_21_d), .S(slice_block_4_y1));
  NFET nfet_22 (.G(load_over), .D(nfet_22_d), .S(slice_block_4_y2));
  NFET nfet_23 (.G(load_over), .D(nfet_23_d), .S(slice_block_5_y1));
  NFET nfet_24 (.G(load_over), .D(nfet_24_d), .S(slice_block_5_y2));
  NFET nfet_25 (.G(load_over), .D(nfet_25_d), .S(slice_block_6_y1));
  NFET nfet_26 (.G(load_over), .D(nfet_26_d), .S(slice_block_6_y2));
  switch_block switch_block_33 (
    .R(switch_block_33_r), .L(connection_box_19_u3), .D(switch_block_33_d), .clk(clk_t),
    .Si(switch_block_37_so), .So(c19));  // open: U
  connection_box connection_box_21 (
    .in(nfet_21_d), .Si(c26), .clk(clk_t), .u0(switch_block_33_d), .d0(connection_box_21_d0),
    .u1(connection_box_21_u1), .d1(connection_box_21_d1), .u2(connection_box_21_u2),
    .d2(connection_box_21_d2), .u3(connection_box_21_u3), .d3(connection_box_21_d3), .So(c27));
  connection_box connection_box_22 (
    .in(nfet_22_d), .Si(c27), .clk(clk_t), .u0(connection_box_21_d0), .d0(connection_box_22_d0),
    .u1(connection_box_21_d1), .d1(connection_box_22_d1), .u2(connection_box_21_d2),
    .d2(connection_box_22_d2), .u3(connection_box_21_d3), .d3(connection_box_22_d3), .So(d1));
  switch_block switch_block_34 (
    .R(switch_block_34_r), .L(switch_block_18_r), .U(connection_box_22_d0), .D(switch_block_34_d),
    .clk(clk_t), .Si(switch_block_38_so), .So(s7));
  connection_box connection_box_23 (
    .in(nfet_23_d), .Si(c32), .clk(clk_t), .u0(switch_block_34_d), .d0(connection_box_23_d0),
    .u1(connection_box_23_u1), .d1(connection_box_23_d1), .u2(connection_box_23_u2),
    .d2(connection_box_23_d2), .u3(connection_box_23_u3), .d3(connection_box_23_d3), .So(c33));
  connection_box connection_box_24 (
    .in(nfet_24_d), .Si(c33), .clk(clk_t), .u0(connection_box_23_d0), .d0(connection_box_24_d0),
    .u1(connection_box_23_d1), .d1(connection_box_24_d1), .u2(connection_box_23_d2),
    .d2(connection_box_24_d2), .u3(connection_box_23_d3), .d3(connection_box_24_d3), .So(d4));
  switch_block switch_block_35 (
    .R(switch_block_35_r), .L(switch_block_19_r), .U(connection_box_24_d0), .D(switch_block_35_d),
    .clk(clk_t), .Si(switch_block_39_so), .So(s11));
  connection_box connection_box_25 (
    .in(nfet_25_d), .Si(c38), .clk(clk_t), .u0(switch_block_35_d), .d0(connection_box_25_d0),
    .u1(connection_box_25_u1), .d1(connection_box_25_d1), .u2(connection_box_25_u2),
    .d2(connection_box_25_d2), .u3(connection_box_25_u3), .d3(connection_box_25_d3), .So(c39));
  connection_box connection_box_26 (
    .in(nfet_26_d), .Si(c39), .clk(clk_t), .u0(connection_box_25_d0), .d0(connection_box_26_d0),
    .u1(connection_box_25_d1), .d1(connection_box_26_d1), .u2(connection_box_25_d2),
    .d2(connection_box_26_d2), .u3(connection_box_25_d3), .d3(connection_box_26_d3), .So(d7));
  switch_block switch_block_36 (
    .R(switch_block_36_r), .L(connection_box_20_d0), .U(connection_box_26_d0), .clk(clk_t),
    .Si(switch_block_40_so), .So(c10));  // open: D
  switch_block switch_block_37 (
    .R(switch_block_37_r), .L(connection_box_19_u2), .D(connection_box_21_u1), .clk(clk_t),
    .Si(switch_block_41_so), .So(switch_block_37_so));  // open: U
  switch_block switch_block_38 (
    .R(switch_block_38_r), .L(switch_block_22_r), .U(connection_box_22_d1), .D(connection_box_23_u1),
    .clk(clk_t), .Si(switch_block_42_so), .So(switch_block_38_so));
  switch_block switch_block_39 (
    .R(switch_block_39_r), .L(switch_block_23_r), .U(connection_box_24_d1), .D(connection_box_25_u1),
    .clk(clk_t), .Si(switch_block_43_so), .So(switch_block_39_so));
  switch_block switch_block_40 (
    .R(switch_block_40_r), .L(connection_box_20_d1), .U(connection_box_26_d1), .clk(clk_t),
    .Si(switch_block_44_so), .So(switch_block_40_so));  // open: D
  switch_block switch_block_41 (
    .R(switch_block_41_r), .L(connection_box_19_u1), .D(connection_box_21_u2), .clk(clk_t),
    .Si(switch_block_45_so), .So(switch_block_41_so));  // open: U
  switch_block switch_block_42 (
    .R(switch_block_42_r), .L(switch_block_26_r), .U(connection_box_22_d2), .D(connection_box_23_u2),
    .clk(clk_t), .Si(switch_block_46_so), .So(switch_block_42_so));
  switch_block switch_block_43 (
    .R(switch_block_43_r), .L(switch_block_27_r), .U(connection_box_24_d2), .D(connection_box_25_u2),
    .clk(clk_t), .Si(switch_block_47_so), .So(switch_block_43_so));
  switch_block switch_block_44 (
    .R(switch_block_44_r), .L(connection_box_20_d2), .U(connection_box_26_d2), .clk(clk_t),
    .Si(switch_block_48_so), .So(switch_block_44_so));  // open: D
  switch_block switch_block_45 (
    .R(switch_block_45_r), .L(connection_box_19_u0), .D(connection_box_21_u3), .clk(clk_t), .Si(s2),
    .So(switch_block_45_so));  // open: U
  switch_block switch_block_46 (
    .R(switch_block_46_r), .L(switch_block_30_r), .U(connection_box_22_d3), .D(connection_box_23_u3),
    .clk(clk_t), .Si(s6), .So(switch_block_46_so));
  switch_block switch_block_47 (
    .R(switch_block_47_r), .L(switch_block_31_r), .U(connection_box_24_d3), .D(connection_box_25_u3),
    .clk(clk_t), .Si(s10), .So(switch_block_47_so));
  switch_block switch_block_48 (
    .R(switch_block_48_r), .L(connection_box_20_d3), .U(connection_box_26_d3), .clk(clk_t), .Si(s14),
    .So(switch_block_48_so));  // open: D
  NFET nfet_27 (.G(load_over), .D(p19), .S(nfet_27_s));
  slice_block slice_block_7 (
    .A0(connection_box_21_u3), .A3(connection_box_21_d0), .A1(connection_box_21_d2),
    .A2(connection_box_21_d1), .B0(switch_block_45_r), .B1(connection_box_28_u1), .B2(connection_box_28_u2),
    .B3(connection_box_29_u3), .C0(switch_block_46_r), .C1(switch_block_42_r), .C2(switch_block_38_r),
    .C3(switch_block_34_r), .clk0(switch_block_46_r), .clk1(switch_block_42_r), .clk2(switch_block_38_r),
    .Y1(slice_block_7_y1), .Y2(slice_block_7_y2), .clk(clk_t), .Si(d2), .So(c26), .f_clk(clk));  // open: data
  slice_block slice_block_8 (
    .A0(connection_box_23_u3), .A3(connection_box_23_d0), .A1(connection_box_23_d2),
    .A2(connection_box_23_d1), .B0(switch_block_46_r), .B1(switch_block_42_r), .B2(switch_block_38_r),
    .B3(switch_block_34_r), .C0(switch_block_47_r), .C1(switch_block_43_r), .C2(switch_block_39_r),
    .C3(switch_block_35_r), .clk0(switch_block_47_r), .clk1(switch_block_43_r), .clk2(switch_block_39_r),
    .Y1(slice_block_8_y1), .Y2(slice_block_8_y2), .clk(clk_t), .Si(d5), .So(c32), .f_clk(clk));  // open: data
  slice_block slice_block_9 (
    .A0(connection_box_25_u3), .A3(connection_box_25_d0), .A1(connection_box_25_d2),
    .A2(connection_box_25_d1), .B0(switch_block_47_r), .B1(switch_block_43_r), .B2(switch_block_39_r),
    .B3(switch_block_35_r), .C0(connection_box_27_d3), .C1(connection_box_27_d2), .C2(connection_box_27_d1),
    .C3(connection_box_30_d0), .clk0(switch_block_48_r), .clk1(switch_block_44_r), .clk2(switch_block_40_r),
    .Y1(slice_block_9_y1), .Y2(slice_block_9_y2), .clk(clk_t), .Si(d8), .So(c38), .f_clk(clk));  // open: data
  connection_box connection_box_27 (
    .in(nfet_28_d), .Si(c10), .clk(clk_t), .u0(switch_block_36_r), .d0(connection_box_27_d0),
    .u1(switch_block_40_r), .d1(connection_box_27_d1), .u2(switch_block_44_r), .d2(connection_box_27_d2),
    .u3(switch_block_48_r), .d3(connection_box_27_d3), .So(c11));
  NFET nfet_28 (.G(load_over), .D(nfet_28_d), .S(p10));
  connection_box connection_box_28 (
    .in(nfet_27_s), .Si(c19), .clk(clk_t), .u0(connection_box_28_u0), .d0(switch_block_45_r),
    .u1(connection_box_28_u1), .d1(switch_block_41_r), .u2(connection_box_28_u2), .d2(switch_block_37_r),
    .u3(connection_box_28_u3), .d3(switch_block_33_r), .So(c18));
  NFET nfet_29 (.G(load_over), .D(p18), .S(nfet_29_s));
  connection_box connection_box_29 (
    .in(nfet_29_s), .Si(c18), .clk(clk_t), .u0(connection_box_29_u0), .d0(connection_box_28_u0),
    .u1(connection_box_29_u1), .d1(connection_box_28_u1), .u2(connection_box_29_u2),
    .d2(connection_box_28_u2), .u3(connection_box_29_u3), .d3(connection_box_28_u3), .So(s3));
  connection_box connection_box_30 (
    .in(nfet_30_d), .Si(c11), .clk(clk_t), .u0(connection_box_27_d0), .d0(connection_box_30_d0),
    .u1(connection_box_27_d1), .d1(connection_box_30_d1), .u2(connection_box_27_d2),
    .d2(connection_box_30_d2), .u3(connection_box_27_d3), .d3(connection_box_30_d3), .So(s15));
  NFET nfet_30 (.G(load_over), .D(nfet_30_d), .S(p11));
  NFET nfet_31 (.G(load_over), .D(nfet_31_d), .S(slice_block_7_y1));
  NFET nfet_32 (.G(load_over), .D(nfet_32_d), .S(slice_block_7_y2));
  NFET nfet_33 (.G(load_over), .D(nfet_33_d), .S(slice_block_8_y1));
  NFET nfet_34 (.G(load_over), .D(nfet_34_d), .S(slice_block_8_y2));
  NFET nfet_35 (.G(load_over), .D(nfet_35_d), .S(slice_block_9_y1));
  NFET nfet_36 (.G(load_over), .D(nfet_36_d), .S(slice_block_9_y2));
  switch_block switch_block_49 (
    .L(connection_box_29_u3), .D(switch_block_49_d), .clk(clk_t), .So(c28));  // open: R, U, Si
  connection_box connection_box_31 (
    .in(nfet_31_d), .Si(c28), .clk(clk_t), .u0(switch_block_49_d), .d0(connection_box_31_d0),
    .u1(connection_box_31_u1), .d1(connection_box_31_d1), .u2(connection_box_31_u2),
    .d2(connection_box_31_d2), .u3(connection_box_31_u3), .d3(connection_box_31_d3), .So(c17));
  connection_box connection_box_32 (
    .in(nfet_32_d), .Si(c29), .clk(clk_t), .u0(connection_box_32_u0), .d0(connection_box_32_d0),
    .u1(connection_box_32_u1), .d1(connection_box_32_d1), .u2(connection_box_32_u2),
    .d2(connection_box_32_d2), .u3(connection_box_32_u3), .d3(connection_box_32_d3), .So(d2));
  switch_block switch_block_50 (
    .L(switch_block_34_r), .U(connection_box_32_d0), .D(switch_block_50_d), .clk(clk_t),
    .Si(switch_block_54_so), .So(c34));  // open: R
  connection_box connection_box_33 (
    .in(nfet_33_d), .Si(c34), .clk(clk_t), .u0(switch_block_50_d), .d0(connection_box_33_d0),
    .u1(connection_box_33_u1), .d1(connection_box_33_d1), .u2(connection_box_33_u2),
    .d2(connection_box_33_d2), .u3(connection_box_33_u3), .d3(connection_box_33_d3), .So(c15));
  connection_box connection_box_34 (
    .in(nfet_34_d), .Si(c35), .clk(clk_t), .u0(connection_box_34_u0), .d0(connection_box_34_d0),
    .u1(connection_box_34_u1), .d1(connection_box_34_d1), .u2(connection_box_34_u2),
    .d2(connection_box_34_d2), .u3(connection_box_34_u3), .d3(connection_box_34_d3), .So(d5));
  switch_block switch_block_51 (
    .L(switch_block_35_r), .U(connection_box_34_d0), .D(switch_block_51_d), .clk(clk_t),
    .Si(switch_block_55_so), .So(c40));  // open: R
  connection_box connection_box_35 (
    .in(nfet_35_d), .Si(c40), .clk(clk_t), .u0(switch_block_51_d), .d0(connection_box_35_d0),
    .u1(connection_box_35_u1), .d1(connection_box_35_d1), .u2(connection_box_35_u2),
    .d2(connection_box_35_d2), .u3(connection_box_35_u3), .d3(connection_box_35_d3), .So(c13));
  connection_box connection_box_36 (
    .in(nfet_36_d), .Si(c41), .clk(clk_t), .u0(connection_box_36_u0), .d0(connection_box_36_d0),
    .u1(connection_box_36_u1), .d1(connection_box_36_d1), .u2(connection_box_36_u2),
    .d2(connection_box_36_d2), .u3(connection_box_36_u3), .d3(connection_box_36_d3), .So(d8));
  switch_block switch_block_52 (
    .L(connection_box_30_d0), .U(connection_box_36_d0), .clk(clk_t), .So(out));  // open: R, D, Si
  switch_block switch_block_53 (.L(connection_box_29_u2), .D(connection_box_31_u1), .clk(clk_t));  // open: R, U, cfg
  switch_block switch_block_54 (
    .L(switch_block_38_r), .U(connection_box_32_d1), .D(connection_box_33_u1), .clk(clk_t),
    .Si(switch_block_58_so), .So(switch_block_54_so));  // open: R
  switch_block switch_block_55 (
    .L(switch_block_39_r), .U(connection_box_34_d1), .D(connection_box_35_u1), .clk(clk_t),
    .Si(switch_block_59_so), .So(switch_block_55_so));  // open: R
  switch_block switch_block_56 (.L(connection_box_30_d1), .U(connection_box_36_d1), .clk(clk_t));  // open: R, D, cfg
  switch_block switch_block_57 (.L(connection_box_29_u1), .D(connection_box_31_u2), .clk(clk_t));  // open: R, U, cfg
  switch_block switch_block_58 (
    .L(switch_block_42_r), .U(connection_box_32_d2), .D(connection_box_33_u2), .clk(clk_t),
    .Si(switch_block_62_so), .So(switch_block_58_so));  // open: R
  switch_block switch_block_59 (
    .L(switch_block_43_r), .U(connection_box_34_d2), .D(connection_box_35_u2), .clk(clk_t),
    .Si(switch_block_63_so), .So(switch_block_59_so));  // open: R
  switch_block switch_block_60 (.L(connection_box_30_d2), .U(connection_box_36_d2), .clk(clk_t));  // open: R, D, cfg
  switch_block switch_block_61 (
    .L(connection_box_29_u0), .D(connection_box_31_u3), .clk(clk_t), .Si(s3));  // open: R, U, So
  switch_block switch_block_62 (
    .L(switch_block_46_r), .U(connection_box_32_d3), .D(connection_box_33_u3), .clk(clk_t), .Si(s7),
    .So(switch_block_62_so));  // open: R
  switch_block switch_block_63 (
    .L(switch_block_47_r), .U(connection_box_34_d3), .D(connection_box_35_u3), .clk(clk_t), .Si(s11),
    .So(switch_block_63_so));  // open: R
  switch_block switch_block_64 (
    .L(connection_box_30_d3), .U(connection_box_36_d3), .clk(clk_t), .Si(s15));  // open: R, D, So
  connection_box connection_box_37 (
    .in(nfet_40_s), .Si(c17), .clk(clk_t), .u0(connection_box_37_u0), .d0(connection_box_31_d3),
    .u1(connection_box_37_u1), .d1(connection_box_31_d2), .u2(connection_box_37_u2),
    .d2(connection_box_31_d1), .u3(connection_box_37_u3), .d3(connection_box_31_d0), .So(c16));
  connection_box connection_box_38 (
    .in(nfet_37_d), .Si(c16), .clk(clk_t), .u0(connection_box_32_u3), .d0(connection_box_37_u0),
    .u1(connection_box_32_u2), .d1(connection_box_37_u1), .u2(connection_box_32_u1),
    .d2(connection_box_37_u2), .u3(connection_box_32_u0), .d3(connection_box_37_u3), .So(c29));
  NFET nfet_37 (.G(load_over), .D(nfet_37_d), .S(p16));
  connection_box connection_box_39 (
    .in(nfet_41_s), .Si(c15), .clk(clk_t), .u0(connection_box_39_u0), .d0(connection_box_33_d3),
    .u1(connection_box_39_u1), .d1(connection_box_33_d2), .u2(connection_box_39_u2),
    .d2(connection_box_33_d1), .u3(connection_box_39_u3), .d3(connection_box_33_d0), .So(c14));
  connection_box connection_box_40 (
    .in(nfet_38_d), .Si(c14), .clk(clk_t), .u0(connection_box_34_u3), .d0(connection_box_39_u0),
    .u1(connection_box_34_u2), .d1(connection_box_39_u1), .u2(connection_box_34_u1),
    .d2(connection_box_39_u2), .u3(connection_box_34_u0), .d3(connection_box_39_u3), .So(c35));
  NFET nfet_38 (.G(load_over), .D(nfet_38_d), .S(p14));
  connection_box connection_box_41 (
    .in(nfet_42_s), .Si(c13), .clk(clk_t), .u0(connection_box_41_u0), .d0(connection_box_35_d3),
    .u1(connection_box_41_u1), .d1(connection_box_35_d2), .u2(connection_box_41_u2),
    .d2(connection_box_35_d1), .u3(connection_box_41_u3), .d3(connection_box_35_d0), .So(c12));
  connection_box connection_box_42 (
    .in(nfet_39_d), .Si(c12), .clk(clk_t), .u0(connection_box_36_u3), .d0(connection_box_41_u0),
    .u1(connection_box_36_u2), .d1(connection_box_41_u1), .u2(connection_box_36_u1),
    .d2(connection_box_41_u2), .u3(connection_box_36_u0), .d3(connection_box_41_u3), .So(c41));
  NFET nfet_39 (.G(load_over), .D(nfet_39_d), .S(p12));
  NFET nfet_40 (.G(load_over), .D(p17), .S(nfet_40_s));
  NFET nfet_41 (.G(load_over), .D(p15), .S(nfet_41_s));
  NFET nfet_42 (.G(load_over), .D(p13), .S(nfet_42_s));

  // Other names for the same wires on the sheet: f_clk = clk

  // Notes on the sheet:
  //   clk: Hz: 5000
  //   sys_clk: Hz: 5000
  //   contents of bitstream (hex, n*v repeats v):
  //   1,7*0,1,24*0,1
endmodule
