// Digital circuit johnson_counter.dig as structural Verilog
module johnson_counter (
  input  clk,
  input  clk_2,
  output Q0,
  output Q1,
  output Q2,
  output Q3
);

  fpga_ckt fpga_ckt_1 ();  // open: clk, p0, p1, p2, p3, p4, p5, p6, p7, p8, p9, p10, p11, p12, p13, p14, p15, p16, p17, p18, p19, p20, p21, p22, p23, sys_clk

  // Other names for the same wires on the sheet: sclk = clk_2

  // Notes on the sheet:
  //   clk: Hz: 10
  //   clk_2: Hz: 5000
endmodule
