// Digital circuit register_4bit.dig as structural Verilog
module register_4bit (
  input  D,
  input  clk,
  input  clk_2,
  output Q3,
  output Q2,
  output Q1,
  output Q0
);

  // fpga_ckt fpga_ckt_1: pin names not known; wires that end beside it: D, Q3, Q2, Q1, clk, Q0, clk_2

  // Other names for the same wires on the sheet: sclk = clk_2

  // Notes on the sheet:
  //   clk_2: Hz: 5000
endmodule
