// Digital circuit shift_reg_4bit.dig as structural Verilog
module shift_reg_4bit (
  input  i,
  input  c,
  output o,
  output [3:0] d
);

  D_FF d_ff_1 (.D(i), .C(c), .Q(d[0]));  // open: nQ
  D_FF d_ff_2 (.D(d[0]), .C(c), .Q(d[1]));  // open: nQ
  D_FF d_ff_3 (.D(d[1]), .C(c), .Q(d[2]));  // open: nQ
  D_FF d_ff_4 (.D(d[2]), .C(c), .Q(d[3]));  // open: nQ

  assign o = d[3];
endmodule
