// Digital circuit slice_block.dig as structural Verilog
module slice_block (
  input  A0,
  input  A3,
  input  A1,
  input  A2,
  input  B0,
  input  B1,
  input  B2,
  input  B3,
  input  C0,
  input  C1,
  input  C2,
  input  C3,
  input  clk0,
  input  clk1,
  input  clk2,
  input  clk,
  input  Si,
  input  f_clk,
  output Y1,
  output Y2,
  output So,
  output [35:0] data
);

  wire d_ff_1_q, d_ff_2_q, multiplexer_1_out, multiplexer_2_out, multiplexer_3_out, multiplexer_4_out,
       multiplexer_8_out, multiplexer_9_out, multiplexer_10_out, multiplexer_11_out, multiplexer_12_out,
       multiplexer_13_out, not_1_out, shift_reg_4bit_1_o, shift_reg_4bit_2_o, shift_reg_4bit_3_o,
       shift_reg_4bit_4_o, shift_reg_4bit_5_o, shift_reg_4bit_6_o, shift_reg_4bit_7_o, shift_reg_4bit_8_o;
  wire [2:0] multiplexer_5_out;
  wire [7:0] register_1_q, register_2_q;

  shift_reg_4bit shift_reg_4bit_1 (.i(Si), .c(clk), .o(shift_reg_4bit_1_o), .d(data[3:0]));
  shift_reg_4bit shift_reg_4bit_2 (.i(shift_reg_4bit_1_o), .c(clk), .o(shift_reg_4bit_2_o), .d(data[7:4]));
  shift_reg_4bit shift_reg_4bit_3 (.i(shift_reg_4bit_2_o), .c(clk), .o(shift_reg_4bit_3_o), .d(data[11:8]));
  shift_reg_4bit shift_reg_4bit_4 (.i(shift_reg_4bit_3_o), .c(clk), .o(shift_reg_4bit_4_o), .d(data[15:12]));
  shift_reg_4bit shift_reg_4bit_5 (.i(shift_reg_4bit_4_o), .c(clk), .o(shift_reg_4bit_5_o), .d(data[19:16]));
  shift_reg_4bit shift_reg_4bit_6 (.i(shift_reg_4bit_5_o), .c(clk), .o(shift_reg_4bit_6_o), .d(data[23:20]));
  shift_reg_4bit shift_reg_4bit_7 (.i(shift_reg_4bit_6_o), .c(clk), .o(shift_reg_4bit_7_o), .d(data[27:24]));
  shift_reg_4bit shift_reg_4bit_8 (.i(shift_reg_4bit_7_o), .c(clk), .o(shift_reg_4bit_8_o), .d(data[31:28]));
  shift_reg_4bit shift_reg_4bit_9 (.i(shift_reg_4bit_8_o), .c(clk), .o(So), .d(data[35:32]));
  Multiplexer #(.Selector_Bits(2)) multiplexer_1 (
    .sel(data[7:6]), .in_0(A0), .in_1(A1), .in_2(A2), .in_3(A3), .out(multiplexer_1_out));
  Multiplexer #(.Selector_Bits(2)) multiplexer_2 (
    .sel(data[5:4]), .in_0(B0), .in_1(B1), .in_2(B2), .in_3(B3), .out(multiplexer_2_out));
  Multiplexer #(.Selector_Bits(2)) multiplexer_3 (
    .sel(data[3:2]), .in_0(C0), .in_1(C1), .in_2(C2), .in_3(C3), .out(multiplexer_3_out));
  Multiplexer #(.Selector_Bits(2)) multiplexer_4 (
    .sel(data[1:0]), .in_0(clk0), .in_1(clk1), .in_2(clk2), .in_3(f_clk), .out(multiplexer_4_out));
  Multiplexer multiplexer_5 (.sel(data[14]), .in_0(1'b0), .in_1(multiplexer_1_out), .out(multiplexer_5_out[2]));
  Multiplexer multiplexer_6 (.sel(data[15]), .in_0(1'b0), .in_1(multiplexer_2_out), .out(multiplexer_5_out[1]));
  Multiplexer multiplexer_7 (.sel(data[16]), .in_0(1'b0), .in_1(multiplexer_3_out), .out(multiplexer_5_out[0]));
  Register #(.Bits(8)) register_1 (.D(data[24:17]), .C(f_clk), .en(1'b1), .Q(register_1_q));
  Register #(.Bits(8)) register_2 (.D(data[32:25]), .C(f_clk), .en(1'b1), .Q(register_2_q));
  Multiplexer #(.Selector_Bits(3)) multiplexer_8 (
    .sel(multiplexer_5_out), .in_0(register_1_q[0]), .in_1(register_1_q[1]), .in_2(register_1_q[2]),
    .in_3(register_1_q[3]), .in_4(register_1_q[4]), .in_5(register_1_q[5]), .in_6(register_1_q[6]),
    .in_7(register_1_q[7]), .out(multiplexer_8_out));
  not not_1 (not_1_out, multiplexer_4_out);
  Multiplexer #(.Selector_Bits(3)) multiplexer_9 (
    .sel(multiplexer_5_out), .in_0(register_2_q[0]), .in_1(register_2_q[1]), .in_2(register_2_q[2]),
    .in_3(register_2_q[3]), .in_4(register_2_q[4]), .in_5(register_2_q[5]), .in_6(register_2_q[6]),
    .in_7(register_2_q[7]), .out(multiplexer_9_out));
  Multiplexer multiplexer_10 (.sel(data[12]), .in_0(multiplexer_4_out), .in_1(not_1_out), .out(multiplexer_10_out));
  Multiplexer multiplexer_11 (.sel(data[13]), .in_0(multiplexer_4_out), .in_1(not_1_out), .out(multiplexer_11_out));
  D_FF d_ff_1 (.D(multiplexer_8_out), .C(multiplexer_10_out), .Q(d_ff_1_q));  // open: nQ
  D_FF d_ff_2 (.D(multiplexer_9_out), .C(multiplexer_11_out), .Q(d_ff_2_q));  // open: nQ
  Multiplexer multiplexer_12 (.sel(data[8]), .in_0(multiplexer_8_out), .in_1(d_ff_1_q), .out(multiplexer_12_out));
  Multiplexer multiplexer_13 (.sel(data[9]), .in_0(multiplexer_9_out), .in_1(d_ff_2_q), .out(multiplexer_13_out));
  assign Y1 = data[10] ? multiplexer_12_out : 1'bz;  // Driver driver_1
  assign Y2 = data[11] ? multiplexer_13_out : 1'bz;  // Driver driver_2

  // Other names for the same wires on the sheet: data1[7:0] = data[24:17]; data2[7:0] = data[32:25];
  //   c_used = data[16]; edge1 = data[12]; edge2 = data[13]; a_used = data[14]; b_used = data[15]
endmodule
