// Digital circuit sr_ff.dig as structural Verilog
module sr_ff (
  input  S,
  input  clk,
  input  R,
  input  clk_2,
  input  clk_3,
  output Qb,
  output Q
);

  fpga_ckt fpga_ckt_1 ();  // open: clk, p0, p1, p2, p3, p4, p5, p6, p7, p8, p9, p10, p11, p12, p13, p14, p15, p16, p17, p18, p19, p20, p21, p22, p23

  // Other names for the same wires on the sheet: clk_t = clk_2; sclk = clk_3

  // Notes on the sheet:
  //   clk_3: Hz: 5000
  //   Set the FF or reset the FF before loading the bitstream to avoid the indeterminate state.
endmodule
