// Digital circuit switch_block.dig as structural Verilog
module switch_block (
  input  clk,
  input  Si,
  output R,
  output L,
  output U,
  output D,
  output So
);

  wire dir1, dir2, dir3, dir4, dir5, dir6, s1, s2, s3, s4, s5, s6, shift_reg_4bit_1_o, shift_reg_4bit_2_o;

  shift_reg_4bit shift_reg_4bit_1 (.i(Si), .c(clk), .o(shift_reg_4bit_1_o), .d({s4, s3, s2, s1}));
  shift_reg_4bit shift_reg_4bit_2 (.i(shift_reg_4bit_1_o), .c(clk), .o(shift_reg_4bit_2_o), .d({dir2, dir1, s6, s5}));
  shift_reg_4bit shift_reg_4bit_3 (.i(shift_reg_4bit_2_o), .c(clk), .o(So), .d({dir6, dir5, dir4, dir3}));
  bidir_buf bidir_buf_1 (.left(L), .right(U), .dir(dir1), .en(s1));
  bidir_buf bidir_buf_2 (.left(D), .right(L), .dir(dir4), .en(s4));
  bidir_buf bidir_buf_3 (.left(L), .right(R), .dir(dir5), .en(s5));
  bidir_buf bidir_buf_4 (.left(U), .right(D), .dir(dir6), .en(s6));
  bidir_buf bidir_buf_5 (.left(U), .right(R), .dir(dir2), .en(s2));
  bidir_buf bidir_buf_6 (.left(R), .right(D), .dir(dir3), .en(s3));
endmodule
